# Fritzing sketch di_day_robot_IoT (saved by Fritzing 0.9.9b)
breadboards: 1

parts:
  M1 = STM32F103C8T6 blue mini board
  Part1 = InvenSense MPU6050
  S1 = Toggle Switch spst [package=THT]
  L298N1 = L298N DC motor driver
  M5 = DC Motor  # not connected
  M7 = DC Motor  # not connected
  M8 = DC Motor  # not connected
  M9 = DC Motor  # not connected
  M10 = RioRand LM2596
  VCC2 = Battery
  HC-SR04_Sensor_1 = HC-SR04 Ultrasonic Distance Sensor
  U1 = NodeMCU V1.0
  HC-SR04_Sensor_2 = HC-SR04 Ultrasonic Distance Sensor
  M11 = fc-51 [package=THT]

nets:
  N1: M1.B12, HC-SR04_Sensor_2.ECHO
  N2: M1.B13, HC-SR04_Sensor_2.TRIG
  N3: M1.A8, M11.pin1
  N4: M1.A9, U1.TX
  N5: M1.A10, U1.RX
  N6: M1.B6, Part1.SCL
  N7: M1.B7, Part1.SDA
  GND: M1.G, M1.GND, Part1.GND, L298N1.GND, M10.Pin_4, HC-SR04_Sensor_1.GND, U1.GND, HC-SR04_Sensor_2.GND, M11.pin2
  VCC: M1.3.3V, M1.3.3, Part1.VCC, M10.Pin_3, HC-SR04_Sensor_1.VCC, U1.Vin, HC-SR04_Sensor_2.VCC, M11.pin3
  N8: M1.A2, L298N1.ENB
  N9: M1.A3, L298N1.IN4
  N10: M1.A4, L298N1.IN3
  N11: M1.A5, L298N1.IN2
  N12: M1.A6, L298N1.IN1
  N13: M1.A7, L298N1.ENA
  N14: M1.B10, HC-SR04_Sensor_1.ECHO
  N15: M1.B11, HC-SR04_Sensor_1.TRIG
  N16: S1.L1, VCC2.+
  N17: S1.COM, M10.Pin_1
  N18: M10.Pin_2, VCC2.-

custom parts:
  Toggle Switch spst: Toggle Switch single pole single throw
  L298N DC motor driver: 2x DC motor driver with 78M05 positive voltage regulator (7..35 V) L298N: max 46 V, 2 A Set 5 V Enable jumper to enable 5 V regultor (needed for the L298N) and +5 V output at screw terminal or supply external +5 V at screw terminal Set ENA and/or ENB to +5 V to enable motor permanently or supply ENA and/or ENB with PWM signal IN1 and IN2 set rotation directory for motor A (OUT1/OUT2) IN2 and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
  NodeMCU V1.0: ESP8266 based NodeMCU
